// Logisim project 8bit_computer.circ as structural Verilog
module ALU (
  input  [7:0] Register_A,
  input  [7:0] Register_B,
  input  [2:0] Flag_register,
  input  [3:0] OP_code,
  output carry,
  output parity,
  output zero,
  output [7:0] Acc
);

  wire not_2_out, subtraktor_1_burrow, subtraktor_2_burrow, sumator_1_flag_c_out, sumator_2_flag_c_out,
       zero_check_1_zero_flag;
  wire [7:0] and_1_out, multiplier_1_out, not_1_out, or_1_out, subtraktor_1_sub, subtraktor_2_sub,
       sumator_1_sum, sumator_2_sum, undriven, xor_1_out;

  Multiplier multiplier_1 (.a(Register_A), .b(Register_B), .out(multiplier_1_out), .cin(undriven));  // open: cout
  assign and_1_out = Register_A & Register_B;  // AND_Gate and_1, 8 bits wide
  assign not_1_out = ~Register_A;  // NOT_Gate not_1, 8 bits wide
  sumator sumator_1 (
    .Flag_C(Flag_register[2]), .A(Register_A), .B(Register_B), .sum(sumator_1_sum),
    .Flag_C_out(sumator_1_flag_c_out));
  subtraktor subtraktor_1 (.A(Register_A), .B(Register_B), .sub(subtraktor_1_sub), .Burrow(subtraktor_1_burrow));
  sumator sumator_2 (
    .Flag_C(Flag_register[2]), .A(Register_A), .B(8'h1), .sum(sumator_2_sum),
    .Flag_C_out(sumator_2_flag_c_out));
  subtraktor subtraktor_2 (.A(Register_A), .B(8'h1), .sub(subtraktor_2_sub), .Burrow(subtraktor_2_burrow));
  assign or_1_out = Register_A | Register_B;  // OR_Gate or_1, 8 bits wide
  assign xor_1_out = Register_A;  // XOR_Gate xor_1, 8 bits wide XOR_Gate
  zero_check zero_check_1 (.acc_in(undriven), .zero_flag(zero_check_1_zero_flag));
  Multiplexer #(.select(4), .width(8)) multiplexer_1 (
    .in0(sumator_1_sum), .in1(subtraktor_1_sub), .in2(sumator_2_sum), .in3(subtraktor_2_sub),
    .in4(multiplier_1_out), .in6(and_1_out), .in7(or_1_out), .in8(xor_1_out), .in9(not_1_out), .out(Acc),
    .sel(OP_code));  // open: in5, in10, in11, in12, in13, in14, in15
  not not_2 (not_2_out, zero_check_1_zero_flag);
  Multiplexer #(.select(4)) multiplexer_2 (
    .in0(sumator_1_flag_c_out), .in1(subtraktor_1_burrow), .in2(sumator_2_flag_c_out),
    .in3(subtraktor_2_burrow), .in4(not_2_out), .out(carry), .sel(OP_code));  // open: in5, in6, in7, in8, in9, in10, in11, in12, in13, in14, in15
  ones_counter ones_counter_1 (.B_in(Acc), .Parity(parity));
  zero_check zero_check_2 (.acc_in(Acc), .zero_flag(zero));
endmodule

module sumator (
  input  Flag_C,
  input  [7:0] A,
  input  [7:0] B,
  output [7:0] sum,
  output Flag_C_out
);

  wire full_adder_1bit_1_carry, full_adder_1bit_2_carry, full_adder_1bit_3_carry, full_adder_1bit_4_carry,
       full_adder_1bit_5_carry, full_adder_1bit_6_carry, full_adder_1bit_7_carry;

  full_adder_1bit full_adder_1bit_1 (.A(A[0]), .B(B[0]), .in_3(Flag_C), .Sum(sum[0]), .Carry(full_adder_1bit_1_carry));
  full_adder_1bit full_adder_1bit_2 (
    .A(A[1]), .B(B[1]), .in_3(full_adder_1bit_1_carry), .Sum(sum[1]), .Carry(full_adder_1bit_2_carry));
  full_adder_1bit full_adder_1bit_3 (
    .A(A[2]), .B(B[2]), .in_3(full_adder_1bit_2_carry), .Sum(sum[2]), .Carry(full_adder_1bit_3_carry));
  full_adder_1bit full_adder_1bit_4 (
    .A(A[3]), .B(B[3]), .in_3(full_adder_1bit_3_carry), .Sum(sum[3]), .Carry(full_adder_1bit_4_carry));
  full_adder_1bit full_adder_1bit_5 (
    .A(A[4]), .B(B[4]), .in_3(full_adder_1bit_4_carry), .Sum(sum[4]), .Carry(full_adder_1bit_5_carry));
  full_adder_1bit full_adder_1bit_6 (
    .A(A[5]), .B(B[5]), .in_3(full_adder_1bit_5_carry), .Sum(sum[5]), .Carry(full_adder_1bit_6_carry));
  full_adder_1bit full_adder_1bit_7 (
    .A(A[6]), .B(B[6]), .in_3(full_adder_1bit_6_carry), .Sum(sum[6]), .Carry(full_adder_1bit_7_carry));
  full_adder_1bit full_adder_1bit_8 (
    .A(A[7]), .B(B[7]), .in_3(full_adder_1bit_7_carry), .Sum(sum[7]), .Carry(Flag_C_out));
endmodule

module full_adder_1bit (
  input  A,
  input  B,
  input  in_3,
  output Sum,
  output Carry
);

  wire and_1_out, and_2_out, or_1_out, xor_1_out;

  xor xor_1 (xor_1_out, A, B);
  and and_1 (and_1_out, B, A);
  or or_1 (or_1_out, B, A);
  and and_2 (and_2_out, in_3, or_1_out);
  xor xor_2 (Sum, xor_1_out, in_3);
  or or_2 (Carry, and_1_out, and_2_out);
endmodule

module subtraktor (
  input  [7:0] A,
  input  [7:0] B,
  output [7:0] sub,
  output Burrow
);

  wire full_subtractor_1_borrow, full_subtractor_2_borrow, full_subtractor_3_borrow,
       full_subtractor_4_borrow, full_subtractor_5_borrow, full_subtractor_6_borrow, full_subtractor_7_borrow;

  full_subtractor full_subtractor_1 (.A(A[0]), .B(B[0]), .Cin(1'b0), .sum(sub[0]), .Borrow(full_subtractor_1_borrow));
  full_subtractor full_subtractor_2 (
    .A(A[1]), .B(B[1]), .Cin(full_subtractor_1_borrow), .sum(sub[1]), .Borrow(full_subtractor_2_borrow));
  full_subtractor full_subtractor_3 (
    .A(A[2]), .B(B[2]), .Cin(full_subtractor_2_borrow), .sum(sub[2]), .Borrow(full_subtractor_3_borrow));
  full_subtractor full_subtractor_4 (
    .A(A[3]), .B(B[3]), .Cin(full_subtractor_3_borrow), .sum(sub[3]), .Borrow(full_subtractor_4_borrow));
  full_subtractor full_subtractor_5 (
    .A(A[4]), .B(B[4]), .Cin(full_subtractor_4_borrow), .sum(sub[4]), .Borrow(full_subtractor_5_borrow));
  full_subtractor full_subtractor_6 (
    .A(A[5]), .B(B[5]), .Cin(full_subtractor_5_borrow), .sum(sub[5]), .Borrow(full_subtractor_6_borrow));
  full_subtractor full_subtractor_7 (
    .A(A[6]), .B(B[6]), .Cin(full_subtractor_6_borrow), .sum(sub[6]), .Borrow(full_subtractor_7_borrow));
  full_subtractor full_subtractor_8 (.A(A[7]), .B(B[7]), .Cin(full_subtractor_7_borrow), .sum(sub[7]), .Borrow(Burrow));
endmodule

module full_subtractor (
  input  A,
  input  B,
  input  Cin,
  output sum,
  output Borrow
);

  wire and_1_out, and_2_out, and_3_out, not_1_out, or_1_out, xor_1_out;

  xor xor_1 (xor_1_out, A, B);
  not not_1 (not_1_out, A);
  and and_1 (and_1_out, not_1_out, Cin);
  and and_2 (and_2_out, not_1_out, B);
  and and_3 (and_3_out, B, Cin);
  xor xor_2 (sum, xor_1_out, Cin);
  or or_1 (or_1_out, and_1_out, and_2_out);
  or or_2 (Borrow, or_1_out, and_3_out);
endmodule

module ones_counter (
  input  [7:0] B_in,
  output Parity
);

  wire xor_1_out, xor_2_out, xor_3_out, xor_4_out, xor_5_out, xor_6_out;

  xor xor_1 (xor_1_out, B_in[0], B_in[1]);
  xor xor_2 (xor_2_out, B_in[2], B_in[3]);
  xor xor_3 (xor_3_out, B_in[4], B_in[5]);
  xor xor_4 (xor_4_out, B_in[6], B_in[7]);
  xor xor_5 (xor_5_out, xor_1_out, xor_2_out);
  xor xor_6 (xor_6_out, xor_3_out, xor_4_out);
  xor xor_7 (Parity, xor_5_out, xor_6_out);
endmodule

module zero_check (
  input  [7:0] acc_in,
  output zero_flag
);

  wire and_1_out, and_2_out, and_3_out, and_4_out, and_5_out, and_6_out, and_7_out, and_8_out, or_1_out;

  and and_1 (and_1_out, acc_in[0], 1'b1);
  and and_2 (and_2_out, acc_in[1], 1'b1);
  and and_3 (and_3_out, acc_in[2], 1'b1);
  and and_4 (and_4_out, acc_in[3], 1'b1);
  and and_5 (and_5_out, acc_in[4], 1'b1);
  and and_6 (and_6_out, acc_in[5], 1'b1);
  and and_7 (and_7_out, acc_in[6], 1'b1);
  and and_8 (and_8_out, acc_in[7], 1'b1);
  or or_1 (or_1_out, and_1_out, and_2_out, and_3_out, and_4_out, and_5_out, and_6_out, and_7_out, and_8_out);
  not not_1 (zero_flag, or_1_out);
endmodule

module main (
  input  in_1,
  output [7:0] out_2
);

  wire cl_out, control_unit_1_acc_enable, control_unit_1_bus_mmr, control_unit_1_flags_enable,
       control_unit_1_mmr_enable, control_unit_1_read_enable, control_unit_1_reg_1_bus,
       control_unit_1_reg_1_enable, control_unit_1_reg_2_bus, control_unit_1_reg_2_enable,
       control_unit_1_reg_3_bus, control_unit_1_reg_3_enable, control_unit_1_reg_4_bus,
       control_unit_1_reg_4_enable, control_unit_1_reg_5_bus, control_unit_1_reg_5_enable,
       control_unit_1_reg_a_bus, control_unit_1_reg_a_enable, control_unit_1_reg_acc_bus,
       control_unit_1_reg_b_bus, control_unit_1_reg_b_enable, control_unit_1_write_enable, not_1_out;
  wire [2:0] alu_1_carry, FLAGS_q;
  wire [3:0] control_unit_1_alu;
  wire [7:0] A_q, ACC_q, alu_1_acc, B_q, control_unit_1_mmr_address, control_unit_1_pc,
       controlled_buffer_8_out, ram_1_dout, REGISTER_1_q, REGISTER_2_q, REGISTER_3_q, REGISTER_4_q,
       REGISTER_5_q;

  Clock cl (.out(cl_out));
  Register A (.D(out_2), .en(control_unit_1_reg_a_enable), .clk(cl_out), .Q(A_q), .clr(in_1));
  Register B (.D(out_2), .en(control_unit_1_reg_b_enable), .clk(cl_out), .Q(B_q), .clr(in_1));
  assign out_2 = control_unit_1_reg_b_bus ? B_q : 8'bz;  // Controlled_Buffer controlled_buffer_1
  Register REGISTER_1 (.D(out_2), .en(control_unit_1_reg_1_enable), .clk(cl_out), .Q(REGISTER_1_q), .clr(in_1));
  assign out_2 = control_unit_1_reg_a_bus ? A_q : 8'bz;  // Controlled_Buffer controlled_buffer_2
  assign out_2 = control_unit_1_reg_1_bus ? REGISTER_1_q : 8'bz;  // Controlled_Buffer controlled_buffer_3
  Register REGISTER_2 (.D(out_2), .en(control_unit_1_reg_2_enable), .clk(cl_out), .Q(REGISTER_2_q), .clr(in_1));
  assign out_2 = control_unit_1_reg_2_bus ? REGISTER_2_q : 8'bz;  // Controlled_Buffer controlled_buffer_4
  Register #(.width(3)) FLAGS (
    .D(alu_1_carry), .en(control_unit_1_flags_enable), .clk(cl_out), .Q(FLAGS_q), .clr(in_1));
  ALU alu_1 (
    .Register_A(A_q), .Register_B(B_q), .Flag_register(FLAGS_q), .OP_code(control_unit_1_alu),
    .carry(alu_1_carry[0]), .parity(alu_1_carry[1]), .zero(alu_1_carry[2]), .Acc(alu_1_acc));
  Register ACC (.D(alu_1_acc), .en(control_unit_1_acc_enable), .clk(cl_out), .Q(ACC_q), .clr(in_1));
  Register REGISTER_3 (.D(out_2), .en(control_unit_1_reg_3_enable), .clk(cl_out), .Q(REGISTER_3_q), .clr(in_1));
  assign out_2 = control_unit_1_reg_acc_bus ? ACC_q : 8'bz;  // Controlled_Buffer controlled_buffer_5
  assign out_2 = control_unit_1_reg_3_bus ? REGISTER_3_q : 8'bz;  // Controlled_Buffer controlled_buffer_6
  Register REGISTER_4 (.D(out_2), .en(control_unit_1_reg_4_enable), .clk(cl_out), .Q(REGISTER_4_q), .clr(in_1));
  assign out_2 = control_unit_1_reg_4_bus ? REGISTER_4_q : 8'bz;  // Controlled_Buffer controlled_buffer_7
  Control_Unit control_unit_1 (
    .reset(in_1), .DATA_BUS(out_2), .clock(cl_out), .flags(FLAGS_q), .PC(control_unit_1_pc),
    .WRITE_ENABLE(control_unit_1_write_enable), .bus_mmr(control_unit_1_bus_mmr),
    .READ_ENABLE(control_unit_1_read_enable), .reg_1_enable(control_unit_1_reg_1_enable),
    .mmr_address(control_unit_1_mmr_address), .mmr_enable(control_unit_1_mmr_enable),
    .reg_2_enable(control_unit_1_reg_2_enable), .reg_3_enable(control_unit_1_reg_3_enable),
    .reg_4_enable(control_unit_1_reg_4_enable), .reg_5_enable(control_unit_1_reg_5_enable),
    .reg_A_enable(control_unit_1_reg_a_enable), .reg_B_enable(control_unit_1_reg_b_enable),
    .reg_1_bus(control_unit_1_reg_1_bus), .reg_2_bus(control_unit_1_reg_2_bus),
    .reg_3_bus(control_unit_1_reg_3_bus), .reg_4_bus(control_unit_1_reg_4_bus),
    .reg_5_bus(control_unit_1_reg_5_bus), .reg_A_bus(control_unit_1_reg_a_bus),
    .reg_B_bus(control_unit_1_reg_b_bus), .reg_ACC_bus(control_unit_1_reg_acc_bus), .ALU(control_unit_1_alu),
    .ACC_enable(control_unit_1_acc_enable), .FLAGS_enable(control_unit_1_flags_enable));
  Register REGISTER_5 (.D(out_2), .en(control_unit_1_reg_5_enable), .clk(cl_out), .Q(REGISTER_5_q), .clr(in_1));
  not not_1 (not_1_out, control_unit_1_mmr_enable);
  assign controlled_buffer_8_out = not_1_out ? control_unit_1_pc : 8'bz;  // Controlled_Buffer controlled_buffer_8
  assign controlled_buffer_8_out = control_unit_1_mmr_enable ? control_unit_1_mmr_address : 8'bz;  // Controlled_Buffer controlled_buffer_9
  assign out_2 = control_unit_1_reg_5_bus ? REGISTER_5_q : 8'bz;  // Controlled_Buffer controlled_buffer_10
  RAM ram_1 (
    .addr(controlled_buffer_8_out), .we(control_unit_1_write_enable), .oe(control_unit_1_read_enable),
    .clk(cl_out), .din(out_2), .dout(ram_1_dout));
  assign out_2 = control_unit_1_bus_mmr ? ram_1_dout : 8'bz;  // Controlled_Buffer controlled_buffer_11
endmodule

module Control_Unit (
  input  reset,
  input  [7:0] DATA_BUS,
  input  clock,
  input  [2:0] flags,
  output [7:0] PC,
  output WRITE_ENABLE,
  output bus_mmr,
  output READ_ENABLE,
  output reg_1_enable,
  output [7:0] mmr_address,
  output mmr_enable,
  output reg_2_enable,
  output reg_3_enable,
  output reg_4_enable,
  output reg_5_enable,
  output reg_A_enable,
  output reg_B_enable,
  output reg_1_bus,
  output reg_2_bus,
  output reg_3_bus,
  output reg_4_bus,
  output reg_5_bus,
  output reg_A_bus,
  output reg_B_bus,
  output reg_ACC_bus,
  output [3:0] ALU,
  output ACC_enable,
  output FLAGS_enable
);

  wire dekoder_1_bus_mmr, dekoder_1_mmr_enable, dekoder_1_next_state, dekoder_1_pc_inp_enable,
       dekoder_1_read_enable, dekoder_1_reg_1_enable, dekoder_1_reg_2_enable, dekoder_1_reg_3_enable,
       dekoder_1_reg_4_enable, dekoder_1_reg_5_enable, dekoder_1_reg_a_enable, dekoder_1_reg_b_enable,
       fetch_1_next_state, fetch_1_pc_enable, fetch_1_read_enable, fsm_1_decode, fsm_1_execute,
       fsm_1_fetch_1, fsm_1_fetch_2, or_3_out;
  wire [7:0] dekoder_1_mmr_address, dekoder_1_pc_input;
  wire [15:0] fetch_1_ins;

  program_counter program_counter_1 (
    .PC_Enable(fetch_1_pc_enable), .inp(dekoder_1_pc_input), .input_enable(dekoder_1_pc_inp_enable),
    .clock(clock), .reset(reset), .outt(PC));
  or or_1 (bus_mmr, dekoder_1_bus_mmr, fsm_1_fetch_2);
  or or_2 (READ_ENABLE, fetch_1_read_enable, dekoder_1_read_enable);
  or or_3 (or_3_out, fetch_1_next_state, dekoder_1_next_state);
  buf or_4 (reg_1_enable, dekoder_1_reg_1_enable);  // OR_Gate
  assign mmr_address = dekoder_1_mmr_address;  // OR_Gate or_5, 8 bits wide OR_Gate
  FSM fsm_1 (
    .I(or_3_out), .RESET(reset), .clock(clock), .fetch_1(fsm_1_fetch_1), .fetch_2(fsm_1_fetch_2),
    .decode(fsm_1_decode), .execute(fsm_1_execute));
  Fetch fetch_1 (
    .START_FETCH_2(fsm_1_fetch_2), .START_FETCH_1(fsm_1_fetch_1), .OP_CODE(DATA_BUS), .RESET(reset),
    .clock(clock), .NEXT_STATE(fetch_1_next_state), .READ_ENABLE(fetch_1_read_enable),
    .PC_enable(fetch_1_pc_enable), .INS(fetch_1_ins));
  buf or_6 (mmr_enable, dekoder_1_mmr_enable);  // OR_Gate
  or or_7 (reg_2_enable, dekoder_1_reg_2_enable, 1'b0);
  or or_8 (reg_3_enable, dekoder_1_reg_3_enable, 1'b0);
  DEKODER dekoder_1 (
    .execute(fsm_1_execute), .DECODE(fsm_1_decode), .INS(fetch_1_ins), .clock(clock), .zero_flag(flags[2]),
    .NEXT_STATE(dekoder_1_next_state), .READ_ENABLE(dekoder_1_read_enable), .bus_mmr(dekoder_1_bus_mmr),
    .mmr_address(dekoder_1_mmr_address), .reg_1_enable(dekoder_1_reg_1_enable),
    .mmr_enable(dekoder_1_mmr_enable), .reg_2_enable(dekoder_1_reg_2_enable),
    .reg_3_enable(dekoder_1_reg_3_enable), .reg_4_enable(dekoder_1_reg_4_enable),
    .reg_5_enable(dekoder_1_reg_5_enable), .reg_A_enable(dekoder_1_reg_a_enable),
    .reg_B_enable(dekoder_1_reg_b_enable), .WRITE_ENABLE(WRITE_ENABLE), .reg_1_bus(reg_1_bus),
    .reg_2_bus(reg_2_bus), .reg_3_bus(reg_3_bus), .reg_4_bus(reg_4_bus), .reg_5_bus(reg_5_bus),
    .reg_A_bus(reg_A_bus), .reg_B_bus(reg_B_bus), .reg_ACC_bus(reg_ACC_bus), .ALU(ALU),
    .ACC_enable(ACC_enable), .PC_INPUT(dekoder_1_pc_input), .PC_INP_ENABLE(dekoder_1_pc_inp_enable),
    .FLAGS_enable(FLAGS_enable));
  or or_9 (reg_4_enable, dekoder_1_reg_4_enable, 1'b0);
  or or_10 (reg_5_enable, dekoder_1_reg_5_enable, 1'b0);
  or or_11 (reg_A_enable, dekoder_1_reg_a_enable, 1'b0);
  or or_12 (reg_B_enable, dekoder_1_reg_b_enable, 1'b0);
endmodule

module program_counter (
  input  PC_Enable,
  input  [7:0] inp,
  input  input_enable,
  input  clock,
  input  reset,
  output [7:0] outt
);

  wire not_1_out, not_2_out;
  wire [7:0] adder_1_out, controlled_buffer_1_out, controlled_buffer_3_out;

  not not_1 (not_1_out, input_enable);
  assign controlled_buffer_1_out = not_1_out ? controlled_buffer_3_out : 8'bz;  // Controlled_Buffer controlled_buffer_1
  assign controlled_buffer_1_out = input_enable ? inp : 8'bz;  // Controlled_Buffer controlled_buffer_2
  Register register_1 (.D(controlled_buffer_1_out), .clk(clock), .Q(outt), .clr(reset));  // open: en
  not not_2 (not_2_out, PC_Enable);
  assign controlled_buffer_3_out = not_2_out ? outt : 8'bz;  // Controlled_Buffer controlled_buffer_3
  assign controlled_buffer_3_out = PC_Enable ? adder_1_out : 8'bz;  // Controlled_Buffer controlled_buffer_4
  Adder adder_1 (.a(outt), .b(8'h1), .out(adder_1_out));  // open: cin, cout
endmodule

module Fetch (
  input  START_FETCH_2,
  input  START_FETCH_1,
  input  [7:0] OP_CODE,
  input  RESET,
  input  clock,
  output NEXT_STATE,
  output READ_ENABLE,
  output PC_enable,
  output [15:0] INS
);

  wire controlled_buffer_1_out, controlled_buffer_2_out, controlled_buffer_4_out, ins_1b_1_f2out,
       ins_1b_1_pc_enable, ins_2b_1_f2out, ins_2b_1_next_state, ins_2b_1_pc_enable, ins_len_dec_1_ins_2b,
       ins_len_dec_1_is_byte2nd, not_1_out, not_2_out, not_3_out, or_1_out, or_2_out;
  wire [7:0] ins_len_dec_1_ins;
  wire [15:0] controlled_buffer_3_out, ins_1b_1_instruction, ins_2b_1_ir;

  not not_1 (not_1_out, START_FETCH_1);
  INS_LEN_DEC ins_len_dec_1 (
    .F1(START_FETCH_2), .OPCODE(OP_CODE), .clock(clock), .RESET(RESET),
    .IS_BYTE2ND(ins_len_dec_1_is_byte2nd), .INS_2B(ins_len_dec_1_ins_2b), .INS(ins_len_dec_1_ins));
  Multiplexer multiplexer_1 (.in0(START_FETCH_1), .in1(or_2_out), .out(NEXT_STATE), .sel(not_1_out));
  not not_2 (not_2_out, ins_len_dec_1_ins_2b);
  assign controlled_buffer_1_out = or_1_out ? START_FETCH_2 : 1'bz;  // Controlled_Buffer controlled_buffer_1
  or or_1 (or_1_out, ins_len_dec_1_is_byte2nd, ins_len_dec_1_ins_2b);
  assign controlled_buffer_2_out = not_2_out ? START_FETCH_2 : 1'bz;  // Controlled_Buffer controlled_buffer_2
  INS_2B ins_2b_1 (
    .F2(controlled_buffer_1_out), .is_Byte_2nd(ins_len_dec_1_is_byte2nd), .OPCODE(ins_len_dec_1_ins),
    .clock(clock), .RESET(RESET), .NEXT_STATE(ins_2b_1_next_state), .PC_ENABLE(ins_2b_1_pc_enable),
    .F2out(ins_2b_1_f2out), .IR(ins_2b_1_ir));
  not not_3 (not_3_out, or_1_out);
  or or_2 (or_2_out, ins_1b_1_pc_enable, ins_2b_1_next_state);
  assign controlled_buffer_3_out = or_1_out ? ins_2b_1_ir : 16'bz;  // Controlled_Buffer controlled_buffer_3
  assign controlled_buffer_4_out = or_1_out ? ins_2b_1_f2out : 1'bz;  // Controlled_Buffer controlled_buffer_4
  assign controlled_buffer_4_out = not_3_out ? ins_1b_1_f2out : 1'bz;  // Controlled_Buffer controlled_buffer_5
  assign controlled_buffer_3_out = not_3_out ? ins_1b_1_instruction : 16'bz;  // Controlled_Buffer controlled_buffer_6
  INS_1B ins_1b_1 (
    .f2(controlled_buffer_2_out), .OP_CODE(ins_len_dec_1_ins), .PC_enable(ins_1b_1_pc_enable),
    .F2out(ins_1b_1_f2out), .instruction(ins_1b_1_instruction));
  assign PC_enable = or_1_out ? ins_2b_1_pc_enable : 1'bz;  // Controlled_Buffer controlled_buffer_7
  Register #(.width(16)) IR (
    .D(controlled_buffer_3_out), .en(controlled_buffer_4_out), .clk(clock), .Q(INS), .clr(RESET));
  assign PC_enable = not_3_out ? ins_1b_1_pc_enable : 1'bz;  // Controlled_Buffer controlled_buffer_8

  assign READ_ENABLE = START_FETCH_1;
endmodule

module FSM (
  input  I,
  input  RESET,
  input  clock,
  output fetch_1,
  output fetch_2,
  output decode,
  output execute
);

  wire and_1_out, and_2_out, and_3_out, and_4_out, not_1_out, not_2_out, or_1_out, or_2_out, or_3_out, Q0_qn,
       Q1_qn;
  wire [1:0] Q1_q;

  not not_1 (not_1_out, I);
  and and_1 (and_1_out, Q1_qn, I);
  and and_2 (and_2_out, Q1_q[1], Q1_q[0], not_1_out);
  or or_1 (or_1_out, Q1_qn, not_2_out);
  not not_2 (not_2_out, I);
  or or_2 (or_2_out, and_1_out, and_2_out);
  and and_3 (and_3_out, Q1_q[1], or_1_out);
  and and_4 (and_4_out, I, Q1_q[0], Q0_qn);
  or or_3 (or_3_out, and_3_out, and_4_out);
  D_Flip_Flop Q1 (.D(or_2_out), .clk(clock), .Q(Q1_q[0]), .Qn(Q1_qn), .reset(RESET));  // open: preset
  D_Flip_Flop Q0 (.D(or_3_out), .clk(clock), .Q(Q1_q[1]), .Qn(Q0_qn), .reset(RESET));  // open: preset
  Demultiplexer #(.select(2)) demultiplexer_1 (
    .out0(fetch_1), .out1(fetch_2), .out2(decode), .out3(execute), .in(1'b1), .sel(Q1_q));
endmodule

module INS_1B (
  input  f2,
  input  [7:0] OP_CODE,
  output PC_enable,
  output F2out,
  output [15:0] instruction
);

  assign instruction[15:8] = f2 ? OP_CODE : 8'bz;  // Controlled_Buffer controlled_buffer_1

  assign F2out = f2;
  assign instruction[7:0] = {8{1'b0}};
  assign PC_enable = f2;
endmodule

module INS_2B (
  input  F2,
  input  is_Byte_2nd,
  input  [7:0] OPCODE,
  input  clock,
  input  RESET,
  output NEXT_STATE,
  output PC_ENABLE,
  output F2out,
  output [15:0] IR
);

  wire [7:0] controlled_buffer_2_out;

  assign IR[7:0] = is_Byte_2nd ? OPCODE : 8'bz;  // Controlled_Buffer controlled_buffer_1
  assign controlled_buffer_2_out = F2 ? OPCODE : 8'bz;  // Controlled_Buffer controlled_buffer_2
  and and_1 (NEXT_STATE, is_Byte_2nd, F2);
  Register register_1 (.D(controlled_buffer_2_out), .en(F2), .clk(clock), .Q(IR[15:8]), .clr(RESET));
  and and_2 (F2out, F2, is_Byte_2nd);

  assign PC_ENABLE = F2;
endmodule

module INS_LEN_DEC (
  input  F1,
  input  [7:0] OPCODE,
  input  clock,
  input  RESET,
  output IS_BYTE2ND,
  output INS_2B,
  output [7:0] INS
);

  wire and_2_out, d_ff_1_q, or_1_out;

  or or_1 (or_1_out, OPCODE[4], OPCODE[5], OPCODE[6]);
  and and_1 (INS_2B, or_1_out, OPCODE[7]);
  and and_2 (and_2_out, F1, INS_2B);
  D_Flip_Flop d_ff_1 (.D(and_2_out), .clk(clock), .Q(d_ff_1_q), .reset(RESET));  // open: Qn, preset
  D_Flip_Flop d_ff_2 (.D(d_ff_1_q), .clk(clock), .Q(IS_BYTE2ND), .reset(RESET));  // open: Qn, preset

  assign INS = OPCODE;
endmodule

module FETCH_BACKUP (
  input  START_FETCH_2,
  input  START_FETCH_1,
  input  [7:0] OP_CODE,
  input  RESET,
  input  clock,
  output NEXT_STATE,
  output READ_ENABLE,
  output PC_enable,
  output [15:0] INS
);

  wire ins_1b_1_f2out, not_1_out;
  wire [15:0] ins_1b_1_instruction;

  not not_1 (not_1_out, START_FETCH_1);
  Multiplexer multiplexer_1 (.in0(START_FETCH_1), .in1(START_FETCH_2), .out(NEXT_STATE), .sel(not_1_out));
  INS_1B ins_1b_1 (
    .f2(START_FETCH_2), .OP_CODE(OP_CODE), .PC_enable(PC_enable), .F2out(ins_1b_1_f2out),
    .instruction(ins_1b_1_instruction));
  Register #(.width(16)) IR (.D(ins_1b_1_instruction), .en(ins_1b_1_f2out), .clk(clock), .Q(INS), .clr(RESET));

  assign READ_ENABLE = START_FETCH_1;
endmodule

module FETCH2_BACKUP (
  input  START_FETCH_2,
  input  START_FETCH_1,
  input  [7:0] OPCODE,
  input  RESET,
  input  clock,
  input  in_6,
  input  [7:0] in_7,
  input  in_8,
  input  in_9,
  input  in_10,
  input  [7:0] in_11,
  input  in_12,
  input  in_13,
  input  in_14,
  input  in_15,
  input  in_16,
  input  in_17,
  input  in_18,
  input  in_19,
  input  in_20,
  input  in_21,
  input  in_22,
  input  in_23,
  input  in_24,
  input  in_25,
  input  in_26,
  input  in_27,
  input  in_28,
  input  in_29,
  input  in_30,
  output RESET_STATE,
  output NEXT_STATE,
  output READ_ENABLE,
  output PC_enable,
  output [15:0] INS,
  output [15:0] out_36,
  output WRITE_ENABLE,
  output bus_mmr,
  output enable_A,
  output BUS_A,
  output enable_B,
  output BUS_B,
  output enabe_1,
  output BUS_1,
  output enable_2,
  output BUS_2,
  output enable_3,
  output BUS_3,
  output enable_4,
  output BUS_4,
  output enable_5,
  output BUS_5,
  output enable_ACC,
  output BUS_ACC
);

  wire controlled_buffer_1_out, fetch_1_p6, fetch_1_p7, fetch_1_p8, fetch_1_p9, fsm_1_fetch_1, fsm_1_fetch_2,
       ins_2b_1_f2out, ins_len_dec_1_ins_2b, ins_len_dec_1_is_byte2nd, multiplexer_2_out, not_1_out, or_5_out;
  wire [7:0] ins_len_dec_1_ins, program_counter_1_outt, ram_1_dout;
  wire [15:0] ins_2b_1_ir;

  // OR_Gate or_1 has open pins: in0=in_17, out=open
  // OR_Gate or_2 has open pins: in0=in_18, out=open
  not not_1 (not_1_out, START_FETCH_1);
  // OR_Gate or_3 has open pins: in0=in_14, out=open
  Multiplexer multiplexer_1 (.in0(START_FETCH_1), .in1(START_FETCH_2), .out(NEXT_STATE), .sel(not_1_out));
  INS_LEN_DEC ins_len_dec_1 (
    .F1(START_FETCH_1), .OPCODE(OPCODE), .clock(clock), .RESET(RESET), .IS_BYTE2ND(ins_len_dec_1_is_byte2nd),
    .INS_2B(ins_len_dec_1_ins_2b), .INS(ins_len_dec_1_ins));
  program_counter program_counter_1 (
    .PC_Enable(fetch_1_p9), .inp(in_7), .input_enable(in_8), .clock(in_12), .reset(in_9),
    .outt(program_counter_1_outt));
  // OR_Gate or_4 has open pins: in0=in_19, out=open
  assign controlled_buffer_1_out = or_5_out ? START_FETCH_2 : 1'bz;  // Controlled_Buffer controlled_buffer_1
  or or_5 (or_5_out, ins_len_dec_1_is_byte2nd, ins_len_dec_1_ins_2b);
  RAM ram_1 (.addr(program_counter_1_outt), .we(in_10), .oe(fetch_1_p8), .clk(in_12), .din(in_11), .dout(ram_1_dout));
  // OR_Gate or_6 has open pins: in0=in_15, out=open
  // OR_Gate or_7 has open pins: in0=in_16, out=open
  INS_2B ins_2b_1 (
    .F2(controlled_buffer_1_out), .is_Byte_2nd(ins_len_dec_1_is_byte2nd), .OPCODE(ins_len_dec_1_ins),
    .clock(clock), .RESET(RESET), .NEXT_STATE(RESET_STATE), .PC_ENABLE(PC_enable), .F2out(ins_2b_1_f2out),
    .IR(ins_2b_1_ir));
  // OR_Gate or_8 has open pins: in0=in_13, out=open
  Multiplexer multiplexer_2 (.in0(fetch_1_p6), .in1(in_9), .out(multiplexer_2_out), .sel(in_6));
  // OR_Gate or_9 has open pins: in0=in_20, out=open
  Register #(.width(16)) IR (.D(ins_2b_1_ir), .en(ins_2b_1_f2out), .clk(clock), .Q(INS), .clr(RESET));
  // OR_Gate or_10 has open pins: in0=in_21, out=open
  FSM fsm_1 (
    .I(fetch_1_p7), .RESET(multiplexer_2_out), .clock(in_12), .fetch_1(fsm_1_fetch_1), .fetch_2(fsm_1_fetch_2));  // open: decode, execute
  // OR_Gate or_11 has open pins: in0=in_22, out=open
  // Fetch fetch_1: pin names not known; wires that end beside it: fsm_1_fetch_2, fsm_1_fetch_1, ram_1_dout, in_9, in_12, fetch_1_p6, fetch_1_p7, fetch_1_p8, fetch_1_p9, out_36
  // OR_Gate or_12 has open pins: in0=in_23, out=open
  // OR_Gate or_13 has open pins: in0=in_24, out=open
  // OR_Gate or_14 has open pins: in0=in_25, out=open
  // OR_Gate or_15 has open pins: in0=in_26, out=open
  // OR_Gate or_16 has open pins: in0=in_27, out=open
  // OR_Gate or_17 has open pins: in0=in_28, out=open
  // OR_Gate or_18 has open pins: in0=in_29, out=open
  // OR_Gate or_19 has open pins: in0=in_30, out=open

  assign READ_ENABLE = START_FETCH_1;
endmodule

module MUX_FETCH_CONT (
  input  F1,
  input  clock
);

  wire d_ff_1_qn;

  D_Flip_Flop d_ff_1 (.D(F1), .clk(clock), .Qn(d_ff_1_qn));  // open: Q, preset, reset
endmodule

module DEKODER (
  input  execute,
  input  DECODE,
  input  [15:0] INS,
  input  clock,
  input  zero_flag,
  output NEXT_STATE,
  output READ_ENABLE,
  output bus_mmr,
  output [7:0] mmr_address,
  output reg_1_enable,
  output mmr_enable,
  output reg_2_enable,
  output reg_3_enable,
  output reg_4_enable,
  output reg_5_enable,
  output reg_A_enable,
  output reg_B_enable,
  output WRITE_ENABLE,
  output reg_1_bus,
  output reg_2_bus,
  output reg_3_bus,
  output reg_4_bus,
  output reg_5_bus,
  output reg_A_bus,
  output reg_B_bus,
  output reg_ACC_bus,
  output [3:0] ALU,
  output ACC_enable,
  output [7:0] PC_INPUT,
  output PC_INP_ENABLE,
  output FLAGS_enable
);

  wire and_1_out, and_2_out, and_3_out, and_4_out, and_5_out, and_6_out, comparator_1_lt, comparator_2_gt,
       demultiplexer_1_out9, demultiplexer_1_out10, demultiplexer_1_out11, demultiplexer_1_out12,
       demultiplexer_1_out13, load_ins_1_mmr_enable, load_ins_1_reg_1_enable, load_ins_1_reg_2_enable,
       load_ins_1_reg_3_enable, load_ins_1_reg_4_enable, load_ins_1_reg_5_enable, load_ins_1_reg_a_enable,
       load_ins_1_reg_b_enable, mov_ins_1_reg_1_bus, mov_ins_1_reg_1_enable, mov_ins_1_reg_2_bus,
       mov_ins_1_reg_2_enable, mov_ins_1_reg_3_bus, mov_ins_1_reg_3_enable, mov_ins_1_reg_4_bus,
       mov_ins_1_reg_4_enable, mov_ins_1_reg_5_bus, mov_ins_1_reg_5_enable, mov_ins_1_reg_a_bus,
       mov_ins_1_reg_a_enable, mov_ins_1_reg_acc_bus, mov_ins_1_reg_b_bus, mov_ins_1_reg_b_enable, or_1_out,
       store_ins_1_mmr_enable, store_ins_1_reg_1_bus, store_ins_1_reg_2_bus, store_ins_1_reg_3_bus,
       store_ins_1_reg_4_bus, store_ins_1_reg_5_bus, store_ins_1_reg_a_bus, store_ins_1_reg_acc_bus,
       store_ins_1_reg_b_bus, store_ins_1_write_enable;
  wire [3:0] controlled_buffer_3_out, controlled_buffer_4_out, controlled_buffer_5_out,
       controlled_buffer_6_out;
  wire [7:0] controlled_buffer_2_out, controlled_buffer_7_out, load_ins_1_mmr_address,
       store_ins_1_mmr_address;
  wire [11:0] controlled_buffer_1_out;

  assign {ALU, controlled_buffer_1_out} = or_1_out ? INS : 16'bz;  // Controlled_Buffer controlled_buffer_1
  or or_1 (or_1_out, execute, DECODE);
  Demultiplexer #(.select(4)) demultiplexer_1 (
    .out9(demultiplexer_1_out9), .out10(demultiplexer_1_out10), .out11(demultiplexer_1_out11),
    .out12(demultiplexer_1_out12), .out13(demultiplexer_1_out13), .in(or_1_out), .sel(ALU));  // open: out0, out1, out2, out3, out4, out5, out6, out7, out8, out14, out15
  and and_1 (and_1_out, DECODE, demultiplexer_1_out9);
  and and_2 (and_2_out, execute, demultiplexer_1_out11);
  assign controlled_buffer_2_out = demultiplexer_1_out9 ? controlled_buffer_1_out[7:0] : 8'bz;  // Controlled_Buffer controlled_buffer_2
  assign controlled_buffer_3_out = demultiplexer_1_out11 ? controlled_buffer_1_out[11:8] : 4'bz;  // Controlled_Buffer controlled_buffer_3
  and and_3 (and_3_out, demultiplexer_1_out10, execute);
  assign controlled_buffer_4_out = demultiplexer_1_out10 ? controlled_buffer_1_out[7:4] : 4'bz;  // Controlled_Buffer controlled_buffer_4
  assign controlled_buffer_5_out = demultiplexer_1_out10 ? controlled_buffer_1_out[11:8] : 4'bz;  // Controlled_Buffer controlled_buffer_5
  and and_4 (and_4_out, execute, demultiplexer_1_out13);
  assign controlled_buffer_6_out = demultiplexer_1_out9 ? controlled_buffer_1_out[11:8] : 4'bz;  // Controlled_Buffer controlled_buffer_6
  assign controlled_buffer_7_out = demultiplexer_1_out11 ? controlled_buffer_1_out[7:0] : 8'bz;  // Controlled_Buffer controlled_buffer_7
  Comparator #(.mode("unsigned"), .width(4)) comparator_1 (.a(4'b1010), .b(ALU), .lt(comparator_1_lt));  // open: gt, eq
  assign PC_INPUT = comparator_1_lt ? controlled_buffer_1_out[11:4] : 8'bz;  // Controlled_Buffer controlled_buffer_8
  and and_5 (and_5_out, zero_flag, and_4_out);
  or or_2 (NEXT_STATE, DECODE, execute);
  load_ins load_ins_1 (
    .execute(and_1_out), .chosen_mmr(controlled_buffer_2_out), .chosen_register(controlled_buffer_6_out),
    .clock(clock), .mmr_enable(load_ins_1_mmr_enable), .READ_ENABLE(READ_ENABLE), .bus_mmr(bus_mmr),
    .mmr_address(load_ins_1_mmr_address), .reg_1_enable(load_ins_1_reg_1_enable),
    .reg_2_enable(load_ins_1_reg_2_enable), .reg_3_enable(load_ins_1_reg_3_enable),
    .reg_4_enable(load_ins_1_reg_4_enable), .reg_5_enable(load_ins_1_reg_5_enable),
    .reg_A_enable(load_ins_1_reg_a_enable), .reg_B_enable(load_ins_1_reg_b_enable));
  store_ins store_ins_1 (
    .execute(and_2_out), .chosen_mmr(controlled_buffer_7_out), .chosen_register(controlled_buffer_3_out),
    .mmr_enable(store_ins_1_mmr_enable), .WRITE_ENABLE(store_ins_1_write_enable),
    .mmr_address(store_ins_1_mmr_address), .reg_1_bus(store_ins_1_reg_1_bus),
    .reg_2_bus(store_ins_1_reg_2_bus), .reg_3_bus(store_ins_1_reg_3_bus), .reg_4_bus(store_ins_1_reg_4_bus),
    .reg_5_bus(store_ins_1_reg_5_bus), .reg_A_bus(store_ins_1_reg_a_bus), .reg_B_bus(store_ins_1_reg_b_bus),
    .reg_ACC_bus(store_ins_1_reg_acc_bus));
  mov_ins mov_ins_1 (
    .execute(and_3_out), .reg_to_write(controlled_buffer_4_out), .chosen_register(controlled_buffer_5_out),
    .reg_1_enable(mov_ins_1_reg_1_enable), .reg_2_enable(mov_ins_1_reg_2_enable),
    .reg_3_enable(mov_ins_1_reg_3_enable), .reg_4_enable(mov_ins_1_reg_4_enable),
    .reg_5_enable(mov_ins_1_reg_5_enable), .reg_A_enable(mov_ins_1_reg_a_enable),
    .reg_B_enable(mov_ins_1_reg_b_enable), .reg_1_bus(mov_ins_1_reg_1_bus), .reg_2_bus(mov_ins_1_reg_2_bus),
    .reg_3_bus(mov_ins_1_reg_3_bus), .reg_4_bus(mov_ins_1_reg_4_bus), .reg_5_bus(mov_ins_1_reg_5_bus),
    .reg_A_bus(mov_ins_1_reg_a_bus), .reg_B_bus(mov_ins_1_reg_b_bus), .reg_ACC_bus(mov_ins_1_reg_acc_bus));
  and and_6 (and_6_out, demultiplexer_1_out12, execute);
  Comparator #(.mode("unsigned"), .width(4)) comparator_2 (.a(4'b1001), .b(ALU), .gt(comparator_2_gt));  // open: eq, lt
  assign mmr_address = load_ins_1_mmr_address | store_ins_1_mmr_address;  // OR_Gate or_3, 8 bits wide
  or or_4 (reg_1_enable, load_ins_1_reg_1_enable, mov_ins_1_reg_1_enable);
  or or_5 (mmr_enable, load_ins_1_mmr_enable, store_ins_1_mmr_enable);
  or or_6 (reg_2_enable, load_ins_1_reg_2_enable, mov_ins_1_reg_2_enable);
  or or_7 (reg_3_enable, load_ins_1_reg_3_enable, mov_ins_1_reg_3_enable);
  or or_8 (reg_4_enable, load_ins_1_reg_4_enable, mov_ins_1_reg_4_enable);
  or or_9 (reg_5_enable, load_ins_1_reg_5_enable, mov_ins_1_reg_5_enable);
  or or_10 (reg_A_enable, load_ins_1_reg_a_enable, mov_ins_1_reg_a_enable);
  or or_11 (reg_B_enable, load_ins_1_reg_b_enable, mov_ins_1_reg_b_enable);
  buf or_12 (WRITE_ENABLE, store_ins_1_write_enable);  // OR_Gate
  or or_13 (reg_1_bus, store_ins_1_reg_1_bus, mov_ins_1_reg_1_bus);
  or or_14 (reg_2_bus, store_ins_1_reg_2_bus, mov_ins_1_reg_2_bus);
  or or_15 (reg_3_bus, store_ins_1_reg_3_bus, mov_ins_1_reg_3_bus);
  or or_16 (reg_4_bus, store_ins_1_reg_4_bus, mov_ins_1_reg_4_bus);
  or or_17 (reg_5_bus, store_ins_1_reg_5_bus, mov_ins_1_reg_5_bus);
  or or_18 (reg_A_bus, store_ins_1_reg_a_bus, mov_ins_1_reg_a_bus);
  or or_19 (reg_B_bus, store_ins_1_reg_b_bus, mov_ins_1_reg_b_bus);
  or or_20 (reg_ACC_bus, store_ins_1_reg_acc_bus, mov_ins_1_reg_acc_bus);
  and and_7 (ACC_enable, comparator_2_gt, execute);
  or or_21 (PC_INP_ENABLE, and_6_out, and_5_out);

  assign FLAGS_enable = ACC_enable;
endmodule

module load_ins (
  input  execute,
  input  [7:0] chosen_mmr,
  input  [3:0] chosen_register,
  input  clock,
  output mmr_enable,
  output READ_ENABLE,
  output bus_mmr,
  output [7:0] mmr_address,
  output reg_1_enable,
  output reg_2_enable,
  output reg_3_enable,
  output reg_4_enable,
  output reg_5_enable,
  output reg_A_enable,
  output reg_B_enable
);

  D_Flip_Flop d_ff_1 (.D(execute), .clk(clock), .Q(bus_mmr));  // open: Qn, preset, reset
  Demultiplexer #(.select(4)) demultiplexer_1 (
    .out0(reg_1_enable), .out1(reg_2_enable), .out2(reg_3_enable), .out3(reg_4_enable), .out4(reg_5_enable),
    .out5(reg_A_enable), .out6(reg_B_enable), .in(bus_mmr), .sel(chosen_register));  // open: out7, out8, out9, out10, out11, out12, out13, out14, out15

  assign mmr_address = chosen_mmr;
  assign mmr_enable = execute;
  assign READ_ENABLE = execute;
endmodule

module store_ins (
  input  execute,
  input  [7:0] chosen_mmr,
  input  [3:0] chosen_register,
  output mmr_enable,
  output WRITE_ENABLE,
  output [7:0] mmr_address,
  output reg_1_bus,
  output reg_2_bus,
  output reg_3_bus,
  output reg_4_bus,
  output reg_5_bus,
  output reg_A_bus,
  output reg_B_bus,
  output reg_ACC_bus
);

  Demultiplexer #(.select(4)) demultiplexer_1 (
    .out0(reg_1_bus), .out1(reg_2_bus), .out2(reg_3_bus), .out3(reg_4_bus), .out4(reg_5_bus),
    .out5(reg_A_bus), .out6(reg_B_bus), .out7(reg_ACC_bus), .in(execute), .sel(chosen_register));  // open: out8, out9, out10, out11, out12, out13, out14, out15

  assign mmr_address = chosen_mmr;
  assign mmr_enable = execute;
  assign WRITE_ENABLE = execute;
endmodule

module mov_ins (
  input  execute,
  input  [3:0] reg_to_write,
  input  [3:0] chosen_register,
  output reg_1_enable,
  output reg_2_enable,
  output reg_3_enable,
  output reg_4_enable,
  output reg_5_enable,
  output reg_A_enable,
  output reg_B_enable,
  output reg_1_bus,
  output reg_2_bus,
  output reg_3_bus,
  output reg_4_bus,
  output reg_5_bus,
  output reg_A_bus,
  output reg_B_bus,
  output reg_ACC_bus
);

  Demultiplexer #(.select(4)) demultiplexer_1 (
    .out0(reg_1_enable), .out1(reg_2_enable), .out2(reg_3_enable), .out3(reg_4_enable), .out4(reg_5_enable),
    .out5(reg_A_enable), .out6(reg_B_enable), .in(execute), .sel(reg_to_write));  // open: out7, out8, out9, out10, out11, out12, out13, out14, out15
  Demultiplexer #(.select(4)) demultiplexer_2 (
    .out0(reg_1_bus), .out1(reg_2_bus), .out2(reg_3_bus), .out3(reg_4_bus), .out4(reg_5_bus),
    .out5(reg_A_bus), .out6(reg_B_bus), .out7(reg_ACC_bus), .in(execute), .sel(chosen_register));  // open: out8, out9, out10, out11, out12, out13, out14, out15
endmodule
